# Fritzing sketch Miller (saved by Fritzing 0.9.3b)
breadboards: 1

parts:
  Componente1 = Arduino Mega 2560 (Rev3)
  S1 = H-Bridge with L298N
  GY1 = GY-5150 (MPU-9150) [form="♀ (female)" package=THT]
  hc-sr1 = hc-sr04
  hc-sr2 = hc-sr04
  YwRobot_Power_Supply1 = YwRobot Breadboard Power Supply [part_number=545043]
  M1 = DC Motor
  M2 = DC Motor  # not connected
  VCC1 = Battery block 9V
  M3 = fc-51 [package=THT]
  M4 = fc-51 [package=THT]
  M5 = fc-51 [package=THT]
  J1 = Basic Servo
  U1 = ESP8266 WiFi Module [part_number=ESP8266]
  M6 = fc-51 [package=THT]

nets:
  N1: Componente1.A1, hc-sr2.Trig
  N2: Componente1.A2, hc-sr2.Echo
  N3: Componente1.A7, M6.pin1
  N4: Componente1.D21/SCL, GY1.pin3
  N5: Componente1.D20/SDA, GY1.pin4
  N6: Componente1.D19/RX1, U1.TXD
  N7: Componente1.D18/TX1, U1.RXD
  GND: Componente1.GND, Componente1.VIN, VCC1.-
  N8: Componente1.D11_PWM, J1.pulse
  N9: Componente1.D10_PWM, hc-sr1.Echo
  N10: Componente1.D9_PWM, hc-sr1.Trig
  3V3: Componente1.3V3, U1.VCC, U1.CH_PD
  N11: Componente1.D2_PWM, GY1.pin8
  N12: Componente1.D4_PWM, S1.IN2
  N13: Componente1.D5_PWM, S1.IN1
  N14: Componente1.D6_PWM, S1.IN4
  N15: Componente1.D7_PWM, S1.IN3
  N16: Componente1.D22, M5.pin1
  N17: Componente1.D23, M4.pin1
  N18: Componente1.D53, M3.pin1
  N19: S1.12V, VCC1.+
  N20: S1.OUT4-Motor2, M1.pin_1
  N21: GY1.pin1, hc-sr2.VCC, YwRobot_Power_Supply1.VCC#9, YwRobot_Power_Supply1.VCC#10, M4.pin3, M6.pin3
  N22: GY1.pin2, hc-sr2.GND, YwRobot_Power_Supply1.GND#13, YwRobot_Power_Supply1.GND#14, M4.pin2, M6.pin2
  VCC: hc-sr1.VCC, YwRobot_Power_Supply1.VCC#5, YwRobot_Power_Supply1.VCC#6, M3.pin3, M5.pin3, J1.vcc
  GND_2: hc-sr1.GND, YwRobot_Power_Supply1.GND#11, YwRobot_Power_Supply1.GND#12, M3.pin2, M5.pin2, J1.gnd

custom parts:
  H-Bridge with L298N: h-bridge
  GY-5150 (MPU-9150): Placa GY-5150 basada en conjunto de acelerómetro+giroscopios+magnetómetro MPU-9150
  YwRobot Breadboard Power Supply: The YwRobot Breadboard Power Supply (MB-V2) has two power rails; they can be 5V or 3V3. Power to the module can be provided through the female USB socket or through the A10 (female) 2.1mm power jack.
  ESP8266 WiFi Module: Generic WiFi Module based on the ESP8266 with onboard PCB antenna and UART communications
